# Fritzing sketch Consegna2 (saved by Fritzing 0.9.3b)
breadboards: 1

parts:
  Componente1 = Arduino Uno (Rev3)
  LED1 = smd LED [color="Green (565nm)" package="0805 [SMD]"]
  R1 = Resistor [tolerance=±5% resistance=220 package=THT]
  LED2 = smd LED [color="Green (565nm)" package="0805 [SMD]"]
  R2 = Resistor [tolerance=±5% resistance=220 package=THT]
  R3 = Resistor [tolerance=±5% resistance=220 package=THT]
  S1 = Pushbutton [package="[THT]"]
  S2 = Pushbutton [package="[THT]"]
  R5 = Resistor [tolerance=±5% resistance=10k package=THT]
  R6 = Resistor [tolerance=±5% resistance=10k package=THT]
  LED4 = LED - 5mm [color="Red (633nm)" package="5 mm [THT]"]
  PIR1 = PIR sensor
  U1 = HC-SR04 [chip_label=IC package="SIP (Single Inline) [THT]"]

nets:
  N1: Componente1.D8, U1.Trig
  N2: Componente1.D10_PWM/SS, R3.Pin_0
  N3: Componente1.D11_PWM/MOSI, R1.Pin_0
  N4: Componente1.D12/MISO, R2.Pin_0
  N5: Componente1.D2, PIR1.SIG
  5V: Componente1.D3_PWM, Componente1.D4, Componente1.5V, S1.Pin_1, S1.Pin_2, S1.Pin_3, S1.Pin_4, S2.Pin_1, S2.Pin_2, S2.Pin_3, S2.Pin_4, R5.Pin_1, R6.Pin_1, PIR1.VDD, U1.Vcc
  N6: Componente1.D7, U1.Echo
  GND: Componente1.GND, LED1.cathode, LED2.cathode, R5.Pin_0, R6.Pin_0, LED4.cathode, PIR1.GND, U1.GND
  N7: LED1.anode, R1.Pin_1
  N8: LED2.anode, R2.Pin_1
  N9: R3.Pin_1, LED4.anode

custom parts:
  HC-SR04: HC-SR04 ultrasound distance sensor
