# Fritzing sketch Fritzing (saved by Fritzing 0.9.3b)
breadboards: 1

parts:
  Componente1 = Arduino Uno (Rev3)
  LED1 = smd LED [color="Green (565nm)" package="0805 [SMD]"]
  R1 = Resistor [tolerance=±5% resistance=220 package=THT]
  LED2 = smd LED [color="Green (565nm)" package="0805 [SMD]"]
  S1 = Pushbutton [package="[THT]"]
  S2 = Pushbutton [package="[THT]"]
  R6 = Resistor [tolerance=±5% resistance=10k package=THT]
  LED4 = LED - 5mm [color="Red (633nm)" package="5 mm [THT]"]
  PIR1 = PIR sensor
  U1 = HC-SR04 [chip_label=IC package="SIP (Single Inline) [THT]"]
  R7 = Resistor [tolerance=±5% resistance=220 package=THT]
  R8 = Resistor [tolerance=±5% resistance=220 package=THT]
  R9 = Resistor [tolerance=±5% resistance=10k package=THT]

nets:
  N1: Componente1.D8, U1.Echo
  N2: Componente1.D9_PWM, U1.Trig
  N3: Componente1.D10_PWM/SS, S1.Pin_1, S1.Pin_2, R9.Pin_0
  N4: Componente1.D3_PWM, LED1.anode
  N5: Componente1.D4, LED2.anode
  N6: Componente1.D5_PWM, PIR1.SIG
  N7: Componente1.D6_PWM, LED4.anode
  N8: Componente1.D7, S2.Pin_1, S2.Pin_2, R6.Pin_0
  5V: Componente1.5V, S1.Pin_3, S1.Pin_4, S2.Pin_3, S2.Pin_4, PIR1.VDD, U1.Vcc
  GND: Componente1.GND, R1.Pin_1, R6.Pin_1, PIR1.GND, U1.GND, R7.Pin_1, R8.Pin_1, R9.Pin_1
  N9: LED1.cathode, R1.Pin_0
  N10: LED2.cathode, R7.Pin_0
  N11: LED4.cathode, R8.Pin_0

custom parts:
  HC-SR04: HC-SR04 ultrasound distance sensor
